# Fritzing sketch anemometer (saved by Fritzing 0.9.3b)

parts:
  M1 = DC Motor
  R1 = Resistor [tolerance=±5% resistance=10k package=THT]
  U5 = NodeMCU V3.0
  Part10 = Analog Digital MUX Breakout

nets:
  N1: M1.pin_1, R1.Pin_1, Part10.C2
  3V3: M1.pin_2, U5.3V3, Part10.VCC
  N2: R1.Pin_0, U5.GND#6, U5.GND#16, U5.GND#33, Part10.GND
  N3: U5.D5, Part10.S0
  N4: U5.D6, Part10.S1
  N5: U5.D7, Part10.S2
  N6: U5.D8, Part10.S3
  N7: U5.GND#41, Part10.EN
  N8: U5.A0, Part10.SIG

custom parts:
  NodeMCU V3.0: ESP8266 based NodeMCU
