# Fritzing sketch bme280 (saved by Fritzing 0.9.3b)

parts:
  U2 = NodeMCU V3.0
  BME280_Temp_/_Humidity_/_Air_Pressure1 = BME280 Breakout

nets:
  N1: U2.D1, BME280_Temp_/_Humidity_/_Air_Pressure1.SCK/SCL
  N2: U2.D2, BME280_Temp_/_Humidity_/_Air_Pressure1.SDI/SDA
  3V3: U2.3V3, BME280_Temp_/_Humidity_/_Air_Pressure1.3.3V
  GND: U2.GND, BME280_Temp_/_Humidity_/_Air_Pressure1.GND

custom parts:
  NodeMCU V3.0: ESP8266 based NodeMCU
