# Fritzing sketch rainfall-sensor-testing (saved by Fritzing 0.9.3b)

parts:
  YL-83_-_Detection_Board1 = YL-83 Rain Sensor - Detection Board
  YL-83_-_Control_Board1 = YL-83 Rain Sensor - Control Board
  U4 = NodeMCU V3.0
  Part9 = Analog Digital MUX Breakout

nets:
  N1: YL-83_-_Detection_Board1.POS, YL-83_-_Control_Board1.POS
  N2: YL-83_-_Detection_Board1.NEG, YL-83_-_Control_Board1.NEG
  VCC: YL-83_-_Control_Board1.VCC, U4.3V3, Part9.VCC
  GND: YL-83_-_Control_Board1.GND, U4.GND#6, U4.GND#13, U4.GND#33, Part9.GND
  N3: YL-83_-_Control_Board1.AO, Part9.C1
  N4: U4.D5, Part9.S0
  N5: U4.D6, Part9.S1
  N6: U4.D7, Part9.S2
  N7: U4.D8, Part9.S3
  N8: U4.GND#41, Part9.EN
  N9: U4.A0, Part9.SIG

custom parts:
  YL-83 Rain Sensor - Detection Board: The YL-83 is a rain sensor that has more resistance when dry and less resistance when wet. The module runs at 5V.
  YL-83 Rain Sensor - Control Board: The YL-83 is a rain sensor that has more resistance when dry and less resistance when wet. The module runs at 5V.
  NodeMCU V3.0: ESP8266 based NodeMCU
