# Fritzing sketch testing-sds011 (saved by Fritzing 0.9.3b)

parts:
  Mod3 = SDS011 - dust sensor [part_number=1]
  U2 = NodeMCU V3.0

nets:
  N1: Mod3.5V, U2.VU
  GND: Mod3.GND, U2.GND
  N2: Mod3.RXD, U2.D2
  N3: Mod3.TXD, U2.D1

custom parts:
  SDS011 - dust sensor: The SDS 011 Sensor is a quite recent Air Quality Sensor developed by inovafit, a spin-off from the university of Jinan (in Shandong). With its size, it is probably one of the best sensor in terms of accuracy: While other sensors tend to focus on shrinking the sensor size, the SDS 011 has opted for a size tradeoff allowing it to use a larger fan. And the larger the fan, the better the quality.
  NodeMCU V3.0: ESP8266 based NodeMCU
