# Fritzing sketch uv-sensor-testing (saved by Fritzing 0.9.3b)

parts:
  U2 = NodeMCU V3.0
  UV_Sensor1 = ML8511 UV Sensor Breakout [part_number=SEN-12705]
  Part8 = Analog Digital MUX Breakout

nets:
  3V3: U2.D0, U2.3V3, UV_Sensor1.EN, UV_Sensor1.3.3V, Part8.VCC
  GND: U2.GND#6, U2.RX, U2.GND#13, U2.GND#33, UV_Sensor1.GND, Part8.GND
  N1: U2.D5, Part8.S0
  N2: U2.D6, Part8.S1
  N3: U2.D7, Part8.S2
  N4: U2.D8, Part8.S3
  N5: U2.GND#41, Part8.EN
  N6: U2.A0, Part8.SIG
  N7: UV_Sensor1.OUT, Part8.C0

custom parts:
  NodeMCU V3.0: ESP8266 based NodeMCU
  ML8511 UV Sensor Breakout: Description: The ML8511 breakout is an easy to use ultraviolet light sensor. The MP8511 UV Sensor works by outputing an analog signal in relation to the amount of UV light it detects. This breakout can be very handy in creating devices that warn the user of sunburn or detect the UV index as it relates to weather conditions. This sensor breakout can detect 280-390nm light most effectively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
