# Fritzing sketch uv_sensor_mini_board (saved by Fritzing 0.9.3b)
perfboards: 1

parts:
  J1 = female pin header, 5 pins [form="♀ (female)"]
  J2 = male pin header, 3 pins [form="♂ (male)"]
  J3 = double row female pin header, 2 pins [form="♀ (female)"]  # not connected
  J4 = double row female pin header, 2 pins [form="♀ (female)"]  # not connected
  J5 = female pin header, 3 pins [form="♀ (female)"]
  J6 = female pin header, 3 pins [form="♀ (female)"]
  J7 = female pin header, 3 pins [form="♀ (female)"]
  UV_Sensor1 = ML8511 UV Sensor Breakout  # not connected

nets:
  N1: J1.pin2, J1.pin5, J2.pin3
  N2: J1.pin3, J2.pin2
  N3: J1.pin4, J2.pin1
  N4: J5.pin1, J6.pin1, J7.pin1
  N5: J5.pin2, J6.pin2, J7.pin2
  N6: J5.pin3, J6.pin3, J7.pin3

notes:
  OUT GND VCC
  Short cable from Sensor →
  Cat5 →
  Short cable from weather station →

custom parts:
  ML8511 UV Sensor Breakout: Description: The ML8511 breakout is an easy to use ultraviolet light sensor. The MP8511 UV Sensor works by outputing an analog signal in relation to the amount of UV light it detects. This breakout can be very handy in creating devices that warn the user of sunburn or detect the UV index as it relates to weather conditions. This sensor breakout can detect 280-390nm light most effectively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
