# Fritzing sketch weather-station-board (saved by Fritzing 0.9.3b)
perfboards: 1

parts:
  J1 = female pin header, 3 pins [form="♀ (female)"]  # not connected
  J2 = female pin header, 3 pins [form="♀ (female)"]  # not connected
  J3 = female pin header, 3 pins [form="♀ (female)"]  # not connected
  J4 = female pin header, 1 pin [form="♀ (female)"]  # not connected
  J5 = female pin header, 1 pin [form="♀ (female)"]  # not connected
  J6 = female pin header, 1 pin [form="♀ (female)"]  # not connected
  J7 = female pin header, 1 pin [form="♀ (female)"]  # not connected
  J8 = female pin header, 3 pins [form="♀ (female)"]  # not connected
  J9 = female pin header, 3 pins [form="♀ (female)"]  # not connected
  J10 = female pin header, 3 pins [form="♀ (female)"]  # not connected
  J11 = female pin header, 3 pins [form="♀ (female)"]  # not connected
  J12 = female pin header, 3 pins [form="♀ (female)"]  # not connected
  Existing = female pin header, 5 pins [form="♀ (female)"]
  Rain = female pin header, 3 pins [form="♀ (female)"]
  20cm = female pin header, 3 pins [form="♀ (female)"]
  Existing_2 = female pin header, 2 pins [form="♀ (female)"]
  U2 = NodeMCU V3.0
  J13 = female pin header, 15 pins [form="♀ (female)"]
  J14 = female pin header, 15 pins [form="♀ (female)"]
  Part9 = Analog Digital MUX Breakout
  J15 = female pin header, 8 pins [form="♀ (female)"]
  J16 = female pin header, 16 pins [form="♀ (female)"]
  4-5m? = YL-83 Rain Sensor - Control Board
  Rainfall_Detector = YL-83 Rain Sensor - Detection Board
  UV_Sensor = ML8511 UV Sensor Breakout [part_number=SEN-12705]
  Anemometer = DC Motor
  Mod4 = SDS011 - dust sensor [part_number=1]
  R4 = Resistor [tolerance=±5% resistance=10k package=THT]
  BME280_Temp_/_Humidity_/_Air_Pressure = BME280 Breakout
  20cm_2 = female pin header, 4 pins [form="♀ (female)"]

nets:
  N1: Existing.pin2, J13.pin13, Mod4.5V
  N2: Existing.pin3, Mod4.GND
  N3: Existing.pin4, J14.pin12, Mod4.RXD
  N4: Existing.pin5, J14.pin11, Mod4.TXD
  N5: Rain.pin1, Part9.C1, J16.pin15, 4-5m?.AO
  GND: Rain.pin2, J13.pin6, 4-5m?.GND, BME280_Temp_/_Humidity_/_Air_Pressure.GND, 20cm_2.pin3
  3.3V: Rain.pin3, 20cm.pin1, J13.pin5, J14.pin15, 4-5m?.VCC, UV_Sensor.EN, UV_Sensor.3.3V, BME280_Temp_/_Humidity_/_Air_Pressure.3.3V, 20cm_2.pin4
  N6: 20cm.pin2, UV_Sensor.GND
  N7: 20cm.pin3, Part9.C0, J16.pin16, UV_Sensor.OUT
  N8: Existing_2.pin1, Part9.C2, J16.pin14, Anemometer.pin_1, R4.Pin_0
  N9: Existing_2.pin2, J14.pin10, J15.pin7, Anemometer.pin_2
  N10: U2.GND#6, U2.GND#13, U2.GND#16, U2.GND#33
  N11: J13.pin14, R4.Pin_1
  N12: J13.pin15, J15.pin1
  N13: J14.pin5, J15.pin2
  N14: J14.pin6, J15.pin3
  N15: J14.pin7, J15.pin4
  N16: J14.pin8, J15.pin5
  N17: J14.pin9, J15.pin6, J15.pin8
  N18: J14.pin13, BME280_Temp_/_Humidity_/_Air_Pressure.SDI/SDA, 20cm_2.pin1
  N19: J14.pin14, BME280_Temp_/_Humidity_/_Air_Pressure.SCK/SCL, 20cm_2.pin2
  N20: Part9.C3, J16.pin13
  N21: Part9.C4, J16.pin12
  N22: Part9.C5, J16.pin11
  N23: Part9.C6, J16.pin10
  N24: Part9.C7, J16.pin9
  N25: Part9.C8, J16.pin8
  N26: Part9.C9, J16.pin7
  N27: Part9.C10, J16.pin6
  N28: Part9.C11, J16.pin5
  N29: Part9.C12, J16.pin4
  N30: Part9.C13, J16.pin3
  N31: Part9.C14, J16.pin2
  N32: Part9.C15, J16.pin1
  N33: 4-5m?.POS, Rainfall_Detector.POS
  N34: 4-5m?.NEG, Rainfall_Detector.NEG

custom parts:
  NodeMCU V3.0: ESP8266 based NodeMCU
  YL-83 Rain Sensor - Control Board: The YL-83 is a rain sensor that has more resistance when dry and less resistance when wet. The module runs at 5V.
  YL-83 Rain Sensor - Detection Board: The YL-83 is a rain sensor that has more resistance when dry and less resistance when wet. The module runs at 5V.
  ML8511 UV Sensor Breakout: Description: The ML8511 breakout is an easy to use ultraviolet light sensor. The MP8511 UV Sensor works by outputing an analog signal in relation to the amount of UV light it detects. This breakout can be very handy in creating devices that warn the user of sunburn or detect the UV index as it relates to weather conditions. This sensor breakout can detect 280-390nm light most effectively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
  SDS011 - dust sensor: The SDS 011 Sensor is a quite recent Air Quality Sensor developed by inovafit, a spin-off from the university of Jinan (in Shandong). With its size, it is probably one of the best sensor in terms of accuracy: While other sensors tend to focus on shrinking the sensor size, the SDS 011 has opted for a size tradeoff allowing it to use a larger fan. And the larger the fan, the better the quality.
